# Fritzing sketch Ligações eletronicas Controle de Brassagem (saved by Fritzing 0.9.4)
breadboards: 1

parts:
  GLCD_128x1 = 128 x 64 Graphic LCD
  Componente1 = Arduino Uno (Rev3)
  DS1 = DS18B20 1-Wire Temperature Sensor [part_number=DS18B20]
  DS2 = DS18B20 1-Wire Temperature Sensor [part_number=DS18B20]
  S1 = Momentary Switch [package=ksa_sealed_tac_switch]
  S2 = Momentary Switch [package=ksa_sealed_tac_switch]
  S3 = Momentary Switch [package=ksa_sealed_tac_switch]
  S4 = Momentary Switch [package=ksa_sealed_tac_switch]
  S5 = Momentary Switch [package=ksa_sealed_tac_switch]
  KY-1 = Keyes Relay [package=THT]
  KY-2 = Keyes Relay [package=THT]
  KY-3 = Keyes Relay [package=THT]
  U3 = RELAY-SOLIDSTATE [package=relay-s108t02]
  U4 = RELAY-SOLIDSTATE [package=relay-s108t02]
  R1 = Resistor [tolerance=±5% resistance=4.7k package="0603 [SMD]"]
  R3 = Rotary Potentiometer (Large) [maximum_resistance=100kΩ package=THT]

nets:
  GND: GLCD_128x1.1_Vss, Componente1.A0, Componente1.GND, DS1.GND, DS2.GND, S1.3, S2.3, S3.3, S4.3, S5.3, KY-1.signal, KY-2.signal, KY-3.signal, U3.-, U4.-, R3.leg2
  VDD: GLCD_128x1.2_Vdd, Componente1.5V, DS1.VDD, DS2.VDD, S1.1, S2.1, S3.1, S4.1, S5.1, KY-1.power, KY-2.power, KY-3.power, R1.Pin_1, R3.leg1
  N1: GLCD_128x1.3_Vo, R3.wiper
  N2: GLCD_128x1.4_D/I, Componente1.D5_PWM
  N3: GLCD_128x1.5_R/W, Componente1.D6_PWM
  N4: GLCD_128x1.6_Enable, Componente1.D7
  N5: GLCD_128x1.17_RST, Componente1.D8
  N6: Componente1.D9_PWM, U4.+
  N7: Componente1.D10_PWM/SS, U3.+
  N8: Componente1.D11_PWM/MOSI, DS1.DQ, DS2.DQ, R1.Pin_0
  N9: Componente1.D2, KY-3.ground
  N10: Componente1.D3_PWM, KY-2.ground
  N11: Componente1.D4, KY-1.ground

notes:
  FONTE CHAVEADA 12V
  Bomba
  Motor 1
  Motor 2
  Resistência 1
  Resistência 2
  DS18B20

custom parts:
  Keyes Relay: The Keyes 5V relay module is suitable for SCM development, home appliance control. It uses a 5V~12V TIL control signal which can control DC / AC signal.
